// Logisim project FINAL_PROJECT_MIHIR.circ as structural Verilog: 15 circuits, main circuit main
module main (
  input  [15:0] in_1,
  input  in_2,
  input  in_3,
  input  in_4,
  input  AR_CLR,
  input  in_6,
  input  PC_CLR,
  input  DR_CLR,
  input  TR_INC,
  input  TR_CLR,
  input  in_11,
  output [15:0] out_12,
  output [15:0] out_13,
  output [15:0] out_14,
  output [15:0] OP_AR,
  output [15:0] out_16,
  output [15:0] OP_PC,
  output [15:0] out_18,
  output [15:0] OP_AC,
  output [15:0] out_20,
  output [15:0] OP_DR,
  output [15:0] out_22,
  output [15:0] OP_IR,
  output [15:0] out_24,
  output [15:0] OP_TR
);

  wire A1, A2, A3, A4, A5, A7, AC_CLR, AC_INC, AC_Z, and_1_out, and_2_out, and_3_out, and_4_out, and_5_out,
       and_6_out, and_7_out, and_10_out, and_11_out, and_12_out, and_13_out, and_21_out, and_24_out,
       and_25_out, and_27_out, and_28_out, and_29_out, and_30_out, and_33_out, and_34_out, and_35_out,
       and_41_out, and_42_out, and_43_out, and_44_out, and_45_out, AR_INC, B1, B2, B3, B4, B5, B6, B7, C1,
       C2, C3, C4, C5, C_OUT, D0, D1, D2, D3, D4, D5, D6, D7, d_ff_1_qn, DR_INC, DR_Z, E, LDAC, LDAR, LDDR,
       LDIR, LDPC, LDTR, MEM_WRITE, multiplexer_2_out, not_1_out, not_2_out, not_3_out, not_6_out, not_7_out,
       or_1_out, or_2_out, or_9_out, or_12_out, or_13_out, or_16_out, or_17_out, P, PC_INC, R, RST_CNT, S0,
       S1, S2, T0, T3, T4, T5, T6, T7;
  wire [2:0] ALU_SELECT, counter_1_1_mux_time, priority_encoder_3_out;
  wire [11:0] ADDR;
  wire [15:0] ALU_OUT, multiplexer_1_out;

  not not_1 (not_1_out, OP_IR[15]);
  not not_2 (not_2_out, D7);
  and and_1 (and_1_out, D4, T4);
  and and_2 (and_2_out, D5, T5);
  and and_3 (and_3_out, D5, T4);
  and and_4 (and_4_out, D3, T4);
  and and_5 (and_5_out, P, OP_IR[10]);
  and and_6 (and_6_out, D2, T5);
  and and_7 (and_7_out, D6, T6);
  and and_8 (R, D7, not_1_out, T3);
  and and_9 (P, D7, OP_IR[15], T3);
  or or_1 (or_1_out, D0, D1, D2, D6);
  or or_2 (or_2_out, D3, D5);
  or or_3 (A1, and_1_out, and_2_out);
  or or_4 (A2, T0, and_3_out);
  or or_5 (A3, and_4_out, and_5_out);
  or or_6 (A4, and_6_out, and_7_out);
  and and_10 (and_10_out, not_2_out, OP_IR[15], T3);
  and and_11 (and_11_out, or_1_out, T4);
  and and_12 (and_12_out, or_2_out, T4);
  and and_13 (and_13_out, D6, T6);
  or or_7 (MEM_WRITE, and_12_out, and_13_out);
  or or_8 (A7, and_10_out, and_11_out, LDIR);
  Priority_Encoder priority_encoder_1 (
    .in1(A1), .in2(A2), .in3(A3), .in4(A4), .in5(A5), .in6(in_11), .in7(A7), .out({S2, S1, S0}));  // open: in0, en_in, gs, en_out
  and and_14 (B1, D0, T5);
  and and_15 (B2, D1, T5);
  and and_16 (B3, D2, T5);
  and and_17 (B4, P, OP_IR[11]);
  RAM #(.addrWidth(12), .asyncread("true"), .dataWidth(16)) ram_1 (
    .addr(ADDR), .we(MEM_WRITE), .oe(A7), .clk(in_6), .dout(out_12));  // open: din
  AR ar_1 (.LD(LDAR), .INC(AR_INC), .CLR(AR_CLR), .CLK1(in_6), .IP(multiplexer_1_out), .MUX_IP(OP_AR), .OP_RAM(ADDR));
  PC pc_1 (.LD(LDPC), .INC(PC_INC), .CLR(PC_CLR), .CLK1(in_6), .IP(multiplexer_1_out), .MUX_IP(OP_PC));
  AC ac_1 (.LD(LDAC), .INC(AC_INC), .CLR(AC_CLR), .CLK1(in_6), .IP(ALU_OUT), .MUX_IP(OP_AC));
  DR dr_1 (.LD(LDDR), .INC(DR_INC), .CLR(DR_CLR), .CLK1(in_6), .IP(multiplexer_1_out), .MUX_IP(OP_DR));
  IR ir_1 (.IP(multiplexer_1_out), .LD(LDIR), .CLK1(in_6), .OP(OP_IR));
  TR tr_1 (.LD(LDTR), .INC(TR_INC), .CLR(TR_CLR), .CLK1(in_6), .IP(multiplexer_1_out), .MUX_IP(OP_TR));
  and and_18 (B5, R, OP_IR[9]);
  and and_19 (B6, R, OP_IR[6]);
  and and_20 (B7, R, OP_IR[7]);
  Priority_Encoder priority_encoder_2 (
    .in1(B1), .in2(B2), .in3(B3), .in4(B4), .in5(B5), .in6(B6), .in7(B7), .out(ALU_SELECT));  // open: in0, en_in, gs, en_out
  Multiplexer #(.select(3), .width(16)) multiplexer_1 (
    .in1(OP_AR), .in2(OP_PC), .in3(OP_DR), .in4(OP_AC), .in5(OP_IR), .in6(OP_TR), .in7(out_12),
    .out(multiplexer_1_out), .sel({S2, S1, S0}));  // open: in0
  Decoder #(.enable("false"), .select(3)) decoder_1 (
    .out0(D0), .out1(D1), .out2(D2), .out3(D3), .out4(D4), .out5(D5), .out6(D6), .out7(D7), .sel(OP_IR[14:12]));
  not not_3 (not_3_out, D7);
  and and_21 (and_21_out, not_3_out, OP_IR[15], T3);
  and and_22 (AR_INC, T4, D5);
  or or_9 (or_9_out, D0, D1, D2, D6);
  and and_23 (DR_INC, D6, T5);
  and and_24 (and_24_out, D4, T4);
  and and_25 (and_25_out, D5, T5);
  or or_10 (LDAR, T0, A5, and_21_out);
  and and_26 (LDDR, or_9_out, T4);
  or or_11 (LDPC, and_24_out, and_25_out);
  and and_27 (and_27_out, D3, T4);
  and and_28 (and_28_out, D4, T4);
  and and_29 (and_29_out, D5, T5);
  and and_30 (and_30_out, D6, T6);
  or or_12 (or_12_out, D0, D1, D2);
  or or_13 (or_13_out, OP_IR[6], OP_IR[7], OP_IR[9]);
  and and_31 (AC_CLR, R, OP_IR[11]);
  and and_32 (AC_INC, R, OP_IR[5]);
  and and_33 (and_33_out, or_12_out, T5);
  and and_34 (and_34_out, or_13_out, R);
  and and_35 (and_35_out, P, OP_IR[11]);
  Demultiplexer #(.select(3)) demultiplexer_1 (
    .out0(T0), .out1(LDIR), .out2(A5), .out3(T3), .out4(T4), .out5(T5), .out6(T6), .out7(T7), .in(1'b1),
    .sel(counter_1_1_mux_time));
  COUNTER_1 counter_1_1 (.INR(1'b1), .CLK(in_6), .RST(RST_CNT), .MUX_TIME(counter_1_1_mux_time));
  or or_14 (LDAC, and_33_out, and_34_out, and_35_out);
  or or_15 (RST_CNT, B1, B2, B3, R, P, and_27_out, and_28_out, and_29_out, and_30_out);
  ALU_1 alu_1_1 (
    .ac(OP_AC), .dr(OP_DR), .inpr(in_1), .aluselector(ALU_SELECT), .ipls(in_2), .iprs(in_3),
    .Carry_out(C_OUT), .aluout(ALU_OUT));
  and and_36 (C1, D1, T5);
  and and_37 (C2, R, OP_IR[10]);
  and and_38 (C3, R, OP_IR[8]);
  and and_39 (C4, R, OP_IR[7]);
  and and_40 (C5, R, OP_IR[6]);
  or or_16 (or_16_out, OP_AC[0], OP_AC[1], OP_AC[2], OP_AC[3], OP_AC[4], OP_AC[5], OP_AC[6], OP_AC[7], OP_AC[8], OP_AC[9], OP_AC[10], OP_AC[11], OP_AC[12], OP_AC[13], OP_AC[14], OP_AC[15]);
  or or_17 (or_17_out, OP_DR[0], OP_DR[1], OP_DR[2], OP_DR[3], OP_DR[4], OP_DR[5], OP_DR[6], OP_DR[7], OP_DR[8], OP_DR[9], OP_DR[10], OP_DR[11], OP_DR[12], OP_DR[13], OP_DR[14], OP_DR[15]);
  not not_4 (AC_Z, or_16_out);
  not not_5 (DR_Z, or_17_out);
  not not_6 (not_6_out, OP_AC[15]);
  not not_7 (not_7_out, E);
  Multiplexer #(.select(3)) multiplexer_2 (
    .in0(E), .in1(C_OUT), .in2(in_4), .in3(d_ff_1_qn), .in4(OP_AC[0]), .in5(OP_AC[15]),
    .out(multiplexer_2_out), .sel(priority_encoder_3_out));  // open: in6, in7
  Priority_Encoder priority_encoder_3 (
    .in1(C1), .in2(C2), .in3(C3), .in4(C4), .in5(C5), .out(priority_encoder_3_out));  // open: in0, in6, in7, en_in, gs, en_out
  and and_41 (and_41_out, R, OP_IR[4], not_6_out);
  and and_42 (and_42_out, R, OP_IR[3], OP_AC[15]);
  and and_43 (and_43_out, R, OP_IR[2], AC_Z);
  and and_44 (and_44_out, R, OP_IR[1], not_7_out);
  and and_45 (and_45_out, D6, T6, DR_Z);
  D_Flip_Flop d_ff_1 (.D(multiplexer_2_out), .clk(in_6), .Q(E), .Qn(d_ff_1_qn));  // open: preset, reset
  or or_18 (PC_INC, LDIR, and_41_out, and_42_out, and_43_out, and_44_out, and_45_out);

  assign out_13 = out_12;
  assign out_14 = OP_AR;
  assign out_16 = OP_PC;
  assign out_18 = OP_AC;
  assign out_20 = OP_DR;
  assign out_22 = OP_IR;
  assign out_24 = OP_TR;

  // Other names for the same wires on the sheet: OPIR[15:0] = OP_IR; A6 = in_11; CLK1 = in_6; MEM_READ = A7;
  //   OP_MEM[15:0] = out_12; AC_0 = OP_AC[0]; OPAC[15:0] = OP_AC; AC_15 = OP_AC[15]; OPAR[15:0] = OP_AR;
  //   OPDR[15:0] = OP_DR; b0 = OP_IR[0]; b1_t = OP_IR[1]; b2_t = OP_IR[2]; b3_t = OP_IR[3]; b4_t = OP_IR[4];
  //   b5_t = OP_IR[5]; b6_t = OP_IR[6]; b7_t = OP_IR[7]; b8 = OP_IR[8]; b9 = OP_IR[9]; b10 = OP_IR[10];
  //   b11 = OP_IR[11]; I_BIT = OP_IR[15]; OPPC[15:0] = OP_PC; OPTR[15:0] = OP_TR; T1 = LDIR; T2 = A5
endmodule

module AR (
  input  LD,
  input  INC,
  input  CLR,
  input  CLK1,
  input  [15:0] IP,
  output [15:0] MUX_IP,
  output [11:0] OP_RAM
);

  wire [11:0] adder_1_out, multiplexer_1_out, multiplexer_2_out, multiplexer_3_out;

  Multiplexer #(.width(12)) multiplexer_1 (.in0(MUX_IP[11:0]), .in1(IP[11:0]), .out(multiplexer_1_out), .sel(LD));
  Adder #(.width(12)) adder_1 (.a(MUX_IP[11:0]), .b(12'h1), .out(adder_1_out));  // open: cin, cout
  Multiplexer #(.width(12)) multiplexer_2 (
    .in0(multiplexer_1_out), .in1(adder_1_out), .out(multiplexer_2_out), .sel(INC));
  Multiplexer #(.width(12)) multiplexer_3 (
    .in0(multiplexer_2_out), .in1({12{1'b0}}), .out(multiplexer_3_out), .sel(CLR));
  Register #(.width(12)) register_1 (.D(multiplexer_3_out), .clk(CLK1), .Q(MUX_IP[11:0]));  // open: en, clr

  assign MUX_IP[15:12] = 4'b0000;
  assign OP_RAM = MUX_IP[11:0];
endmodule

module PC (
  input  LD,
  input  INC,
  input  CLR,
  input  CLK1,
  input  [15:0] IP,
  output [15:0] MUX_IP
);

  wire [11:0] adder_1_out, multiplexer_1_out, multiplexer_2_out, multiplexer_3_out;

  Multiplexer #(.width(12)) multiplexer_1 (.in0(MUX_IP[11:0]), .in1(IP[11:0]), .out(multiplexer_1_out), .sel(LD));
  Adder #(.width(12)) adder_1 (.a(MUX_IP[11:0]), .b(12'h1), .out(adder_1_out));  // open: cin, cout
  Multiplexer #(.width(12)) multiplexer_2 (
    .in0(multiplexer_1_out), .in1(adder_1_out), .out(multiplexer_2_out), .sel(INC));
  Multiplexer #(.width(12)) multiplexer_3 (
    .in0(multiplexer_2_out), .in1({12{1'b0}}), .out(multiplexer_3_out), .sel(CLR));
  Register #(.width(12)) register_1 (.D(multiplexer_3_out), .clk(CLK1), .Q(MUX_IP[11:0]));  // open: en, clr

  assign MUX_IP[15:12] = 4'b0000;
endmodule

module IR (
  input  [15:0] IP,
  input  LD,
  input  CLK1,
  output [15:0] OP
);

  wire [15:0] multiplexer_1_out;

  Multiplexer #(.width(16)) multiplexer_1 (.in0(OP), .in1(IP), .out(multiplexer_1_out), .sel(LD));
  Register #(.width(16)) register_1 (.D(multiplexer_1_out), .clk(CLK1), .Q(OP));  // open: en, clr
endmodule

module DR (
  input  LD,
  input  INC,
  input  CLR,
  input  CLK1,
  input  [15:0] IP,
  output [15:0] MUX_IP
);

  wire [15:0] adder_1_out, multiplexer_1_out, multiplexer_2_out, multiplexer_3_out;

  Multiplexer #(.width(16)) multiplexer_1 (.in0(MUX_IP), .in1(IP), .out(multiplexer_1_out), .sel(LD));
  Adder #(.width(16)) adder_1 (.a(MUX_IP), .b(16'h1), .out(adder_1_out));  // open: cin, cout
  Multiplexer #(.width(16)) multiplexer_2 (
    .in0(multiplexer_1_out), .in1(adder_1_out), .out(multiplexer_2_out), .sel(INC));
  Multiplexer #(.width(16)) multiplexer_3 (
    .in0(multiplexer_2_out), .in1({16{1'b0}}), .out(multiplexer_3_out), .sel(CLR));
  Register #(.width(16)) register_1 (.D(multiplexer_3_out), .clk(CLK1), .Q(MUX_IP));  // open: en, clr
endmodule

module AC (
  input  LD,
  input  INC,
  input  CLR,
  input  CLK1,
  input  [15:0] IP,
  output [15:0] MUX_IP
);

  wire [15:0] adder_1_out, multiplexer_1_out, multiplexer_2_out, multiplexer_3_out;

  Multiplexer #(.width(16)) multiplexer_1 (.in0(MUX_IP), .in1(IP), .out(multiplexer_1_out), .sel(LD));
  Adder #(.width(16)) adder_1 (.a(MUX_IP), .b(16'h1), .out(adder_1_out));  // open: cin, cout
  Multiplexer #(.width(16)) multiplexer_2 (
    .in0(multiplexer_1_out), .in1(adder_1_out), .out(multiplexer_2_out), .sel(INC));
  Multiplexer #(.width(16)) multiplexer_3 (
    .in0(multiplexer_2_out), .in1({16{1'b0}}), .out(multiplexer_3_out), .sel(CLR));
  Register #(.width(16)) register_1 (.D(multiplexer_3_out), .clk(CLK1), .Q(MUX_IP));  // open: en, clr
endmodule

module TR (
  input  LD,
  input  INC,
  input  CLR,
  input  CLK1,
  input  [15:0] IP,
  output [15:0] MUX_IP
);

  wire [15:0] adder_1_out, multiplexer_1_out, multiplexer_2_out, multiplexer_3_out;

  Multiplexer #(.width(16)) multiplexer_1 (.in0(MUX_IP), .in1(IP), .out(multiplexer_1_out), .sel(LD));
  Adder #(.width(16)) adder_1 (.a(MUX_IP), .b(16'h1), .out(adder_1_out));  // open: cin, cout
  Multiplexer #(.width(16)) multiplexer_2 (
    .in0(multiplexer_1_out), .in1(adder_1_out), .out(multiplexer_2_out), .sel(INC));
  Multiplexer #(.width(16)) multiplexer_3 (
    .in0(multiplexer_2_out), .in1({16{1'b0}}), .out(multiplexer_3_out), .sel(CLR));
  Register #(.width(16)) register_1 (.D(multiplexer_3_out), .clk(CLK1), .Q(MUX_IP));  // open: en, clr
endmodule

module BIT_ADDER_1 (
  input  CIN,
  input  A,
  input  B,
  input  [1:0] SELECT_LINES,
  output SUM,
  output COUT
);

  wire multiplexer_1_out, not_1_out;

  not not_1 (not_1_out, B);
  Multiplexer #(.select(2)) multiplexer_1 (
    .in0(B), .in1(1'b1), .in2(1'b0), .in3(not_1_out), .out(multiplexer_1_out), .sel(SELECT_LINES));
  Adder #(.width(1)) adder_1 (.a(A), .b(multiplexer_1_out), .out(SUM), .cin(CIN), .cout(COUT));
endmodule

module BIT_ADDER_4 (
  input  CARRY_IN,
  input  [3:0] A,
  input  [3:0] B,
  input  [1:0] SELECT_1,
  output [3:0] SUM,
  output COUT
);

  wire bit_adder_1_1_cout, bit_adder_1_2_cout, bit_adder_1_3_cout;

  BIT_ADDER_1 bit_adder_1_1 (
    .CIN(CARRY_IN), .A(A[0]), .B(B[0]), .SELECT_LINES(SELECT_1), .SUM(SUM[0]), .COUT(bit_adder_1_1_cout));
  BIT_ADDER_1 bit_adder_1_2 (
    .CIN(bit_adder_1_1_cout), .A(A[1]), .B(B[1]), .SELECT_LINES(SELECT_1), .SUM(SUM[1]),
    .COUT(bit_adder_1_2_cout));
  BIT_ADDER_1 bit_adder_1_3 (
    .CIN(bit_adder_1_2_cout), .A(A[2]), .B(B[2]), .SELECT_LINES(SELECT_1), .SUM(SUM[2]),
    .COUT(bit_adder_1_3_cout));
  BIT_ADDER_1 bit_adder_1_4 (
    .CIN(bit_adder_1_3_cout), .A(A[3]), .B(B[3]), .SELECT_LINES(SELECT_1), .SUM(SUM[3]), .COUT(COUT));

  // Other names for the same wires on the sheet: S0 = SUM[0]; S1 = SUM[1]; S2 = SUM[2]; S3 = SUM[3]
endmodule

module BIT_ALU_1 (
  input  A,
  input  B,
  input  [1:0] Select_line,
  output OUT_1
);

  wire and_1_out, nor_1_out, not_1_out, or_1_out;

  and and_1 (and_1_out, A, B);
  or or_1 (or_1_out, A, B);
  nor nor_1 (nor_1_out, A, B);
  not not_1 (not_1_out, A);
  Multiplexer #(.select(2)) multiplexer_1 (
    .in0(and_1_out), .in1(or_1_out), .in2(nor_1_out), .in3(not_1_out), .out(OUT_1), .sel(Select_line));
endmodule

module BIT_ALU_4 (
  input  [3:0] A,
  input  [3:0] B,
  input  [1:0] Select_line,
  output [3:0] OUT_1
);

  BIT_ALU_1 bit_alu_1_1 (.A(A[0]), .B(B[0]), .Select_line(Select_line), .OUT_1(OUT_1[0]));
  BIT_ALU_1 bit_alu_1_2 (.A(A[1]), .B(B[1]), .Select_line(Select_line), .OUT_1(OUT_1[1]));
  BIT_ALU_1 bit_alu_1_3 (.A(A[2]), .B(B[2]), .Select_line(Select_line), .OUT_1(OUT_1[2]));
  BIT_ALU_1 bit_alu_1_4 (.A(A[3]), .B(B[3]), .Select_line(Select_line), .OUT_1(OUT_1[3]));

  // Other names for the same wires on the sheet: O0 = OUT_1[0]; O1 = OUT_1[1]; O2 = OUT_1[2]; O3 = OUT_1[3];
  //   SS[1:0] = Select_line
endmodule

module FINAL_CKT_ALU (
  input  [3:0] A,
  input  [3:0] B,
  input  [3:0] S3S2S1S0,
  input  CIN,
  input  I_R,
  input  I_L,
  output Carry_Out,
  output [3:0] Data_Out
);

  wire [3:0] bit_adder_4_1_sum, bit_alu_4_1_out_1;

  BIT_ADDER_4 bit_adder_4_1 (
    .CARRY_IN(CIN), .A(A), .B(B), .SELECT_1(S3S2S1S0[1:0]), .SUM(bit_adder_4_1_sum), .COUT(Carry_Out));
  BIT_ALU_4 bit_alu_4_1 (.A(A), .B(B), .Select_line(S3S2S1S0[1:0]), .OUT_1(bit_alu_4_1_out_1));
  Multiplexer #(.select(2), .width(4)) multiplexer_1 (
    .in0(bit_adder_4_1_sum), .in1(bit_alu_4_1_out_1), .in2({I_R, A[3:1]}), .in3({A[2:0], I_L}),
    .out(Data_Out), .sel(S3S2S1S0[3:2]));

  // Other names for the same wires on the sheet: S1S0[1:0] = S3S2S1S0[1:0]; S3S2[1:0] = S3S2S1S0[3:2]
endmodule

module SequenceCounter (
  input  INR,
  input  CLK,
  input  RST,
  output [2:0] out_4
);

  wire d_ff_2_qn, d_ff_3_qn;

  D_Flip_Flop d_ff_1 (.D(d_ff_2_qn), .clk(d_ff_2_qn), .Q(out_4[2]), .reset(RST));  // open: Qn, preset
  D_Flip_Flop d_ff_2 (.D(d_ff_3_qn), .clk(out_4[0]), .Q(out_4[1]), .Qn(d_ff_2_qn), .reset(RST));  // open: preset
  D_Flip_Flop d_ff_3 (.D(INR), .clk(CLK), .Q(out_4[0]), .Qn(d_ff_3_qn), .reset(RST));  // open: preset

  // Other names for the same wires on the sheet: D0 = out_4[0]; D1 = out_4[1]; D2 = out_4[2]
endmodule

module COUNTER_1 (
  input  INR,
  input  CLK,
  input  RST,
  output [2:0] MUX_TIME
);

  wire t_ff_1_qn, t_ff_2_qn;

  T_Flip_Flop t_ff_1 (.T(INR), .clk(CLK), .Q(MUX_TIME[0]), .Qn(t_ff_1_qn), .reset(RST));  // open: preset
  T_Flip_Flop t_ff_2 (.T(INR), .clk(t_ff_1_qn), .Q(MUX_TIME[1]), .Qn(t_ff_2_qn), .reset(RST));  // open: preset
  T_Flip_Flop t_ff_3 (.T(INR), .clk(t_ff_2_qn), .Q(MUX_TIME[2]), .reset(RST));  // open: Qn, preset

  // Other names for the same wires on the sheet: T0 = MUX_TIME[0]; T1 = MUX_TIME[1]; T2 = MUX_TIME[2]
endmodule

module ALU_1 (
  input  [15:0] ac,
  input  [15:0] dr,
  input  [15:0] inpr,
  input  [2:0] aluselector,
  input  ipls,
  input  iprs,
  output Carry_out,
  output [15:0] aluout
);

  wire [15:0] adder_1_out, and_1_out, not_1_out;

  assign not_1_out = ~ac;  // NOT_Gate not_1, 16 bits wide
  assign and_1_out = ac & dr;  // AND_Gate and_1, 16 bits wide
  Adder #(.width(16)) adder_1 (.a(ac), .b(dr), .out(adder_1_out), .cin(1'b0), .cout(Carry_out));
  Multiplexer #(.select(3), .width(16)) multiplexer_1 (
    .in1(and_1_out), .in2(adder_1_out), .in3(dr), .in4(inpr), .in5(not_1_out), .in6({iprs, ac[15:1]}),
    .in7({ac[14:0], ipls}), .out(aluout), .sel(aluselector));  // open: in0
endmodule
